// Logisim project 8_bit_instruction_register.circ as structural Verilog: 1 circuit, main circuit main
module main (
  input  in_1,
  input  in_2,
  input  in_3,
  input  in_4,
  input  in_5,
  input  in_6,
  input  in_7,
  input  in_8,
  input  load,
  input  reset,
  input  enable,
  output [7:0] out_12
);

  wire and_1_out, and_2_out, and_3_out, and_4_out, and_5_out, and_6_out, and_7_out, and_8_out, and_9_out,
       and_10_out, and_11_out, and_12_out, and_13_out, and_14_out, and_15_out, and_16_out, clock_1_out,
       d_ff_1_q, d_ff_2_q, d_ff_3_q, d_ff_4_q, d_ff_5_q, d_ff_6_q, d_ff_7_q, d_ff_8_q, not_1_out, or_1_out,
       or_2_out, or_3_out, or_4_out, or_5_out, or_6_out, or_7_out, or_8_out;

  and and_1 (and_1_out, d_ff_1_q, not_1_out);
  Clock clock_1 (.out(clock_1_out));
  and and_2 (and_2_out, in_1, load);
  or or_1 (or_1_out, and_1_out, and_2_out);
  D_Flip_Flop d_ff_1 (.clk(clock_1_out), .D(or_1_out), .Q(d_ff_1_q), .reset(reset));  // open: Qn, preset, en
  assign out_12[7] = enable ? d_ff_1_q : 1'bz;  // Controlled_Buffer controlled_buffer_1
  and and_3 (and_3_out, d_ff_2_q, not_1_out);
  and and_4 (and_4_out, in_2, load);
  or or_2 (or_2_out, and_3_out, and_4_out);
  D_Flip_Flop d_ff_2 (.clk(clock_1_out), .D(or_2_out), .Q(d_ff_2_q), .reset(reset));  // open: Qn, preset, en
  assign out_12[6] = enable ? d_ff_2_q : 1'bz;  // Controlled_Buffer controlled_buffer_2
  and and_5 (and_5_out, d_ff_3_q, not_1_out);
  and and_6 (and_6_out, in_3, load);
  or or_3 (or_3_out, and_5_out, and_6_out);
  and and_7 (and_7_out, in_4, load);
  and and_8 (and_8_out, d_ff_4_q, not_1_out);
  or or_4 (or_4_out, and_8_out, and_7_out);
  D_Flip_Flop d_ff_3 (.clk(clock_1_out), .D(or_3_out), .Q(d_ff_3_q), .reset(reset));  // open: Qn, preset, en
  assign out_12[5] = enable ? d_ff_3_q : 1'bz;  // Controlled_Buffer controlled_buffer_3
  and and_9 (and_9_out, d_ff_5_q, not_1_out);
  or or_5 (or_5_out, and_9_out, and_11_out);
  D_Flip_Flop d_ff_4 (.clk(clock_1_out), .D(or_4_out), .Q(d_ff_4_q), .reset(reset));  // open: Qn, preset, en
  assign out_12[4] = enable ? d_ff_4_q : 1'bz;  // Controlled_Buffer controlled_buffer_4
  and and_10 (and_10_out, d_ff_6_q, not_1_out);
  and and_11 (and_11_out, in_5, load);
  D_Flip_Flop d_ff_5 (.clk(clock_1_out), .D(or_5_out), .Q(d_ff_5_q), .reset(reset));  // open: Qn, preset, en
  assign out_12[3] = enable ? d_ff_5_q : 1'bz;  // Controlled_Buffer controlled_buffer_5
  and and_12 (and_12_out, in_6, load);
  or or_6 (or_6_out, and_10_out, and_12_out);
  D_Flip_Flop d_ff_6 (.clk(clock_1_out), .D(or_6_out), .Q(d_ff_6_q), .reset(reset));  // open: Qn, preset, en
  and and_13 (and_13_out, d_ff_7_q, not_1_out);
  and and_14 (and_14_out, in_7, load);
  or or_7 (or_7_out, and_13_out, and_14_out);
  assign out_12[2] = enable ? d_ff_6_q : 1'bz;  // Controlled_Buffer controlled_buffer_6
  and and_15 (and_15_out, d_ff_8_q, not_1_out);
  or or_8 (or_8_out, and_15_out, and_16_out);
  D_Flip_Flop d_ff_7 (.clk(clock_1_out), .D(or_7_out), .Q(d_ff_7_q), .reset(reset));  // open: Qn, preset, en
  assign out_12[1] = enable ? d_ff_7_q : 1'bz;  // Controlled_Buffer controlled_buffer_7
  and and_16 (and_16_out, in_8, load);
  D_Flip_Flop d_ff_8 (.clk(clock_1_out), .D(or_8_out), .Q(d_ff_8_q), .reset(reset));  // open: Qn, preset, en
  assign out_12[0] = enable ? d_ff_8_q : 1'bz;  // Controlled_Buffer controlled_buffer_8
  not not_1 (not_1_out, load);
endmodule
