// Logisim project AC_msh_mot2keda.circ as structural Verilog: 2 circuits, main circuit main
module main (
  input  reset,
  input  enable,
  input  preset,
  input  EA,
  input  [7:0] in_5,
  input  LA,
  output [7:0] to_add_sub,
  output [7:0] to_the_bus
);

  wire clk_out, D0, D1, D2, D3, D4, D5, D6, D7, not_1_out;

  Clock clk (.out(clk_out));
  D_Flip_Flop d_ff_1 (
    .clk(clk_out), .D(D0), .Q(to_the_bus[0]), .preset(preset), .en(enable), .reset(reset));  // open: Qn
  D_Flip_Flop d_ff_2 (
    .clk(clk_out), .D(D1), .Q(to_the_bus[1]), .preset(preset), .en(enable), .reset(reset));  // open: Qn
  assign to_add_sub = EA ? to_the_bus : 8'bz;  // Controlled_Buffer controlled_buffer_1
  D_Flip_Flop d_ff_3 (
    .clk(clk_out), .D(D2), .Q(to_the_bus[2]), .preset(preset), .en(enable), .reset(reset));  // open: Qn
  D_Flip_Flop d_ff_4 (
    .clk(clk_out), .D(D3), .Q(to_the_bus[3]), .preset(preset), .en(enable), .reset(reset));  // open: Qn
  D_Flip_Flop d_ff_5 (
    .clk(clk_out), .D(D4), .Q(to_the_bus[4]), .preset(preset), .en(enable), .reset(reset));  // open: Qn
  D_Flip_Flop d_ff_6 (
    .clk(clk_out), .D(D5), .Q(to_the_bus[5]), .preset(preset), .en(enable), .reset(reset));  // open: Qn
  D_Flip_Flop d_ff_7 (
    .clk(clk_out), .D(D6), .Q(to_the_bus[6]), .preset(preset), .en(enable), .reset(reset));  // open: Qn
  D_Flip_Flop d_ff_8 (
    .clk(clk_out), .D(D7), .Q(to_the_bus[7]), .preset(preset), .en(enable), .reset(reset));  // open: Qn
  assign {D7, D6, D5, D4, D3, D2, D1, D0} = not_1_out ? in_5 : 8'bz;  // Controlled_Buffer controlled_buffer_2
  not not_1 (not_1_out, LA);

  // Other names for the same wires on the sheet: Q0 = to_the_bus[0]; Q1 = to_the_bus[1]; Q2 = to_the_bus[2];
  //   Q3 = to_the_bus[3]; Q4 = to_the_bus[4]; Q5 = to_the_bus[5]; Q6 = to_the_bus[6]; Q7 = to_the_bus[7]
endmodule

module AC (
);

  main main_1 ();  // open: reset, enable, EA, preset, in_5, to_add_sub, LA, to_the_bus
endmodule
