// Logisim project ALU.circ as structural Verilog: 4 circuits, main circuit main
module main (
  input  cin,
  input  [7:0] A,
  input  [7:0] B,
  input  Eu,
  input  Su,
  output [7:0] AU_out
);

  wire [7:0] adder_1_out, subtractor_1_out;

  Adder adder_1 (.a(A), .b(B), .out(adder_1_out), .cin(cin));  // open: cout
  Subtractor subtractor_1 (.a(A), .b(B), .out(subtractor_1_out), .bin(cin));  // open: bout
  Multiplexer #(.width(8)) multiplexer_1 (.in0(adder_1_out), .in1(subtractor_1_out), .out(AU_out), .sel(Su), .en(Eu));
endmodule

module AU (
  input  cin,
  input  [3:0] A,
  input  [3:0] B,
  input  [1:0] AU_selection,
  input  enable,
  output [3:0] AU_out,
  output status
);

  wire adder_1_cout, subtractor_1_bout;
  wire [3:0] adder_1_out, divider_1_out, multiplier_1_out, subtractor_1_out;

  Adder #(.width(4)) adder_1 (.a(A), .b(B), .out(adder_1_out), .cin(cin), .cout(adder_1_cout));
  Subtractor #(.width(4)) subtractor_1 (.a(A), .b(B), .out(subtractor_1_out), .bin(cin), .bout(subtractor_1_bout));
  Multiplier #(.width(4)) multiplier_1 (.a(A), .b(B), .out(multiplier_1_out));  // open: cin, cout
  Divider #(.width(4)) divider_1 (.a(A), .b(B), .out(divider_1_out));  // open: upper, rem
  Multiplexer #(.select(2), .width(4)) multiplexer_1 (
    .in0(adder_1_out), .in1(subtractor_1_out), .in2(multiplier_1_out), .in3(divider_1_out), .out(AU_out),
    .sel(AU_selection), .en(enable));
  Multiplexer #(.select(2)) multiplexer_2 (
    .in0(adder_1_cout), .in1(subtractor_1_bout), .out(status), .sel(AU_selection), .en(enable));  // open: in2, in3
endmodule

module LU (
  input  [3:0] A,
  input  [3:0] B,
  input  [1:0] LU_selection,
  input  Enable_logic_unit,
  output [3:0] LU_output
);

  wire [3:0] and_1_out, not_1_out, or_1_out, xor_1_out;

  assign and_1_out = A & B;  // AND_Gate and_1, 4 bits wide
  assign or_1_out = A | B;  // OR_Gate or_1, 4 bits wide
  assign xor_1_out = A ^ B;  // XOR_Gate xor_1, 4 bits wide
  assign not_1_out = ~A;  // NOT_Gate not_1, 4 bits wide
  Multiplexer #(.select(2), .width(4)) multiplexer_1 (
    .in0(and_1_out), .in1(or_1_out), .in2(xor_1_out), .in3(not_1_out), .out(LU_output), .sel(LU_selection),
    .en(Enable_logic_unit));
endmodule

module ALU (
  input  cin,
  input  [3:0] A,
  input  [3:0] B,
  input  [1:0] Selection,
  input  enable,
  input  in_6,
  output [3:0] cout,
  output status
);

  wire [3:0] au_1_au_out, lu_1_lu_output;

  AU au_1 (.cin(cin), .A(A), .B(B), .AU_selection(Selection), .status(status), .enable(enable), .AU_out(au_1_au_out));
  LU lu_1 (.A(A), .B(B), .LU_selection(Selection), .Enable_logic_unit(enable), .LU_output(lu_1_lu_output));
  Multiplexer #(.width(4)) multiplexer_1 (.in0(au_1_au_out), .in1(lu_1_lu_output), .out(cout), .sel(in_6));  // open: en
endmodule
