// Logisim project AU.circ as structural Verilog: 1 circuit, main circuit main
module main (
  input  cin,
  input  [3:0] A,
  input  [3:0] B,
  input  [1:0] AU_selection,
  input  enable,
  output [3:0] AU_out,
  output status
);

  wire adder_1_cout, subtractor_1_bout;
  wire [3:0] adder_1_out, divider_1_out, multiplier_1_out, subtractor_1_out;

  Adder #(.width(4)) adder_1 (.a(A), .b(B), .out(adder_1_out), .cin(cin), .cout(adder_1_cout));
  Subtractor #(.width(4)) subtractor_1 (.a(A), .b(B), .out(subtractor_1_out), .bin(cin), .bout(subtractor_1_bout));
  Multiplier #(.width(4)) multiplier_1 (.a(A), .b(B), .out(multiplier_1_out));  // open: cin, cout
  Divider #(.width(4)) divider_1 (.a(A), .b(B), .out(divider_1_out));  // open: upper, rem
  Multiplexer #(.select(2), .width(4)) multiplexer_1 (
    .in0(adder_1_out), .in1(subtractor_1_out), .in2(multiplier_1_out), .in3(divider_1_out), .out(AU_out),
    .sel(AU_selection), .en(enable));
  Multiplexer #(.select(2)) multiplexer_2 (
    .in0(adder_1_cout), .in1(subtractor_1_bout), .out(status), .sel(AU_selection), .en(enable));  // open: in2, in3
endmodule
