// Logisim project PC.circ as structural Verilog: 3 circuits, main circuit main
module main (
  input  cp,
  input  reset,
  input  clk,
  input  ep,
  output [3:0] to_the_bus
);

  wire and_1_out, and_2_out, and_3_out, j_k_ff_1_q, j_k_ff_2_q, j_k_ff_3_q, j_k_ff_4_q, not_1_out;

  not not_1 (not_1_out, clk);
  and and_1 (and_1_out, cp, and_2_out, j_k_ff_2_q);
  J_K_Flip_Flop j_k_ff_1 (
    .J(and_1_out), .clk(not_1_out), .K(and_1_out), .Q(j_k_ff_1_q), .reset(reset));  // open: Qn, preset, en
  assign to_the_bus[3] = ep ? j_k_ff_1_q : 1'bz;  // Controlled_Buffer controlled_buffer_1
  and and_2 (and_2_out, cp, and_3_out, j_k_ff_3_q);
  J_K_Flip_Flop j_k_ff_2 (
    .J(and_2_out), .clk(not_1_out), .K(and_2_out), .Q(j_k_ff_2_q), .reset(reset));  // open: Qn, preset, en
  assign to_the_bus[2] = ep ? j_k_ff_2_q : 1'bz;  // Controlled_Buffer controlled_buffer_2
  and and_3 (and_3_out, cp, j_k_ff_4_q);
  J_K_Flip_Flop j_k_ff_3 (
    .J(and_3_out), .clk(not_1_out), .K(and_3_out), .Q(j_k_ff_3_q), .reset(reset));  // open: Qn, preset, en
  assign to_the_bus[1] = ep ? j_k_ff_3_q : 1'bz;  // Controlled_Buffer controlled_buffer_3
  J_K_Flip_Flop j_k_ff_4 (.J(cp), .clk(not_1_out), .K(cp), .Q(j_k_ff_4_q), .reset(reset));  // open: Qn, preset, en
  assign to_the_bus[0] = ep ? j_k_ff_4_q : 1'bz;  // Controlled_Buffer controlled_buffer_4
endmodule

module pc (
  input  Cp,
  input  Ep,
  output [3:0] to_the_bus
);

  wire clock_1_out, half_adder_1_sum, half_adder_2_carry, half_adder_2_sum, half_adder_3_carry,
       half_adder_3_sum, half_adder_4_carry, half_adder_4_sum, not_1_out;
  wire [3:0] d_ff_4_q;

  not not_1 (not_1_out, clock_1_out);
  Clock clock_1 (.out(clock_1_out));
  half_adder half_adder_1 (.A(half_adder_2_carry), .B(d_ff_4_q[3]), .sum(half_adder_1_sum));  // open: carry
  D_Flip_Flop d_ff_1 (.clk(not_1_out), .D(half_adder_1_sum), .Q(d_ff_4_q[3]));  // open: Qn, preset, en, reset
  half_adder half_adder_2 (.A(half_adder_3_carry), .B(d_ff_4_q[2]), .sum(half_adder_2_sum), .carry(half_adder_2_carry));
  D_Flip_Flop d_ff_2 (.clk(not_1_out), .D(half_adder_2_sum), .Q(d_ff_4_q[2]));  // open: Qn, preset, en, reset
  half_adder half_adder_3 (.A(half_adder_4_carry), .B(d_ff_4_q[1]), .sum(half_adder_3_sum), .carry(half_adder_3_carry));
  D_Flip_Flop d_ff_3 (.clk(not_1_out), .D(half_adder_3_sum), .Q(d_ff_4_q[1]));  // open: Qn, preset, en, reset
  D_Flip_Flop d_ff_4 (.clk(not_1_out), .D(half_adder_4_sum), .Q(d_ff_4_q[0]));  // open: Qn, preset, en, reset
  half_adder half_adder_4 (.A(Cp), .B(d_ff_4_q[0]), .sum(half_adder_4_sum), .carry(half_adder_4_carry));
  assign to_the_bus = Ep ? d_ff_4_q : 4'bz;  // Controlled_Buffer controlled_buffer_1
endmodule

module half_adder (
  input  A,
  input  B,
  output sum,
  output carry
);

  xor xor_1 (sum, A, B);
  and and_1 (carry, A, B);
endmodule
