// Logisim project RAM.circ as structural Verilog: 1 circuit, main circuit main
module main (
  input  [3:0] Address,
  input  [7:0] Data,
  input  nCE,
  output [7:0] Bus
);

  wire not_1_out;

  not not_1 (not_1_out, nCE);
  RAM #(.addrWidth(4), .bus("separate")) ram_1 (
    .addr(Address), .din(Data), .data(Bus), .ld(not_1_out));  // open: str, sel, clk, clr
endmodule
