// Logisim project SAP-1.circ as structural Verilog: 14 circuits, main circuit IR
module IR (
  input  clk,
  input  reset,
  input  Ei,
  input  [7:0] from_the_bus,
  input  Li,
  output [3:0] to_the_bus,
  output [3:0] to_the_controller
);

  wire D0, D1, D2, D3, D4, D5, D6, D7, not_1_out, not_2_out, Q0, Q1, Q2, Q3;

  D_Flip_Flop d_ff_1 (.clk(clk), .D(D7), .Q(to_the_controller[3]), .reset(reset));  // open: Qn, preset, en
  not not_1 (not_1_out, Ei);
  D_Flip_Flop d_ff_2 (.clk(clk), .D(D6), .Q(to_the_controller[2]), .reset(reset));  // open: Qn, preset, en
  assign to_the_bus = not_1_out ? {Q3, Q2, Q1, Q0} : 4'bz;  // Controlled_Buffer controlled_buffer_1
  D_Flip_Flop d_ff_3 (.clk(clk), .D(D5), .Q(to_the_controller[1]), .reset(reset));  // open: Qn, preset, en
  D_Flip_Flop d_ff_4 (.clk(clk), .D(D4), .Q(to_the_controller[0]), .reset(reset));  // open: Qn, preset, en
  D_Flip_Flop d_ff_5 (.clk(clk), .D(D3), .Q(Q3), .reset(reset));  // open: Qn, preset, en
  D_Flip_Flop d_ff_6 (.clk(clk), .D(D2), .Q(Q2), .reset(reset));  // open: Qn, preset, en
  D_Flip_Flop d_ff_7 (.clk(clk), .D(D1), .Q(Q1), .reset(reset));  // open: Qn, preset, en
  D_Flip_Flop d_ff_8 (.clk(clk), .D(D0), .Q(Q0), .reset(reset));  // open: Qn, preset, en
  assign {D7, D6, D5, D4, D3, D2, D1, D0} = not_2_out ? from_the_bus : 8'bz;  // Controlled_Buffer controlled_buffer_2
  not not_2 (not_2_out, Li);

  // Other names for the same wires on the sheet: Q4 = to_the_controller[0]; Q5 = to_the_controller[1];
  //   Q6 = to_the_controller[2]; Q7 = to_the_controller[3]
endmodule

module AC (
  input  clk,
  input  reset,
  input  [7:0] from_the_bus,
  input  LA,
  input  Ea,
  output [7:0] to_add_sub,
  output [7:0] to_the_bus
);

  wire D0, D1, D2, D3, D4, D5, D6, D7, not_1_out;

  D_Flip_Flop d_ff_1 (.clk(clk), .D(D7), .Q(to_add_sub[7]), .reset(reset));  // open: Qn, preset, en
  assign to_the_bus = Ea ? to_add_sub : 8'bz;  // Controlled_Buffer controlled_buffer_1
  D_Flip_Flop d_ff_2 (.clk(clk), .D(D6), .Q(to_add_sub[6]), .reset(reset));  // open: Qn, preset, en
  D_Flip_Flop d_ff_3 (.clk(clk), .D(D5), .Q(to_add_sub[5]), .reset(reset));  // open: Qn, preset, en
  D_Flip_Flop d_ff_4 (.clk(clk), .D(D4), .Q(to_add_sub[4]), .reset(reset));  // open: Qn, preset, en
  D_Flip_Flop d_ff_5 (.clk(clk), .D(D3), .Q(to_add_sub[3]), .reset(reset));  // open: Qn, preset, en
  D_Flip_Flop d_ff_6 (.clk(clk), .D(D2), .Q(to_add_sub[2]), .reset(reset));  // open: Qn, preset, en
  D_Flip_Flop d_ff_7 (.clk(clk), .D(D1), .Q(to_add_sub[1]), .reset(reset));  // open: Qn, preset, en
  assign {D7, D6, D5, D4, D3, D2, D1, D0} = not_1_out ? from_the_bus : 8'bz;  // Controlled_Buffer controlled_buffer_2
  D_Flip_Flop d_ff_8 (.clk(clk), .D(D0), .Q(to_add_sub[0]), .reset(reset));  // open: Qn, preset, en
  not not_1 (not_1_out, LA);

  // Other names for the same wires on the sheet: Q0 = to_add_sub[0]; Q1 = to_add_sub[1]; Q2 = to_add_sub[2];
  //   Q3 = to_add_sub[3]; Q4 = to_add_sub[4]; Q5 = to_add_sub[5]; Q6 = to_add_sub[6]; Q7 = to_add_sub[7]
endmodule

module B_register (
  input  clk,
  input  reset,
  input  Lb,
  input  [7:0] from_the_bus,
  output [7:0] to_the_ALU
);

  wire D0, D1, D2, D3, D4, D5, D6, D7, not_1_out;

  D_Flip_Flop d_ff_1 (.clk(clk), .D(D7), .Q(to_the_ALU[7]), .reset(reset));  // open: Qn, preset, en
  D_Flip_Flop d_ff_2 (.clk(clk), .D(D6), .Q(to_the_ALU[6]), .reset(reset));  // open: Qn, preset, en
  D_Flip_Flop d_ff_3 (.clk(clk), .D(D5), .Q(to_the_ALU[5]), .reset(reset));  // open: Qn, preset, en
  D_Flip_Flop d_ff_4 (.clk(clk), .D(D4), .Q(to_the_ALU[4]), .reset(reset));  // open: Qn, preset, en
  D_Flip_Flop d_ff_5 (.clk(clk), .D(D3), .Q(to_the_ALU[3]), .reset(reset));  // open: Qn, preset, en
  D_Flip_Flop d_ff_6 (.clk(clk), .D(D2), .Q(to_the_ALU[2]), .reset(reset));  // open: Qn, preset, en
  D_Flip_Flop d_ff_7 (.clk(clk), .D(D1), .Q(to_the_ALU[1]), .reset(reset));  // open: Qn, preset, en
  not not_1 (not_1_out, Lb);
  assign {D7, D6, D5, D4, D3, D2, D1, D0} = not_1_out ? from_the_bus : 8'bz;  // Controlled_Buffer controlled_buffer_1
  D_Flip_Flop d_ff_8 (.clk(clk), .D(D0), .Q(to_the_ALU[0]), .reset(reset));  // open: Qn, preset, en

  // Other names for the same wires on the sheet: Q0 = to_the_ALU[0]; Q1 = to_the_ALU[1]; Q2 = to_the_ALU[2];
  //   Q3 = to_the_ALU[3]; Q4 = to_the_ALU[4]; Q5 = to_the_ALU[5]; Q6 = to_the_ALU[6]; Q7 = to_the_ALU[7]
endmodule

module output_register (
  input  clk,
  input  reset,
  input  Lo,
  input  [7:0] from_the_bus,
  output [7:0] to_the_display
);

  wire D0, D1, D2, D3, D4, D5, D6, D7, not_1_out;

  D_Flip_Flop d_ff_1 (.clk(clk), .D(D7), .Q(to_the_display[7]), .reset(reset));  // open: Qn, preset, en
  D_Flip_Flop d_ff_2 (.clk(clk), .D(D6), .Q(to_the_display[6]), .reset(reset));  // open: Qn, preset, en
  D_Flip_Flop d_ff_3 (.clk(clk), .D(D5), .Q(to_the_display[5]), .reset(reset));  // open: Qn, preset, en
  D_Flip_Flop d_ff_4 (.clk(clk), .D(D4), .Q(to_the_display[4]), .reset(reset));  // open: Qn, preset, en
  D_Flip_Flop d_ff_5 (.clk(clk), .D(D3), .Q(to_the_display[3]), .reset(reset));  // open: Qn, preset, en
  D_Flip_Flop d_ff_6 (.clk(clk), .D(D2), .Q(to_the_display[2]), .reset(reset));  // open: Qn, preset, en
  D_Flip_Flop d_ff_7 (.clk(clk), .D(D1), .Q(to_the_display[1]), .reset(reset));  // open: Qn, preset, en
  not not_1 (not_1_out, Lo);
  assign {D7, D6, D5, D4, D3, D2, D1, D0} = not_1_out ? from_the_bus : 8'bz;  // Controlled_Buffer controlled_buffer_1
  D_Flip_Flop d_ff_8 (.clk(clk), .D(D0), .Q(to_the_display[0]), .reset(reset));  // open: Qn, preset, en

  // Other names for the same wires on the sheet: Q0 = to_the_display[0]; Q1 = to_the_display[1];
  //   Q2 = to_the_display[2]; Q3 = to_the_display[3]; Q4 = to_the_display[4]; Q5 = to_the_display[5];
  //   Q6 = to_the_display[6]; Q7 = to_the_display[7]
endmodule

// half_A
module half_adder (
  input  A,
  input  B,
  output sum,
  output carry
);

  xor xor_1 (sum, A, B);
  and and_1 (carry, A, B);
endmodule

// full-A
module full_adder (
  input  from_the_AC,
  input  from_B_register,
  input  carry_in,
  output sum,
  output carry_out
);

  wire and_1_out, and_2_out, xor_1_out;

  xor xor_1 (xor_1_out, from_the_AC, from_B_register);
  and and_1 (and_1_out, from_the_AC, from_B_register);
  xor xor_2 (sum, xor_1_out, carry_in);
  and and_2 (and_2_out, xor_1_out, carry_in);
  or or_1 (carry_out, and_1_out, and_2_out);
endmodule

module ALU (
  input  in_1,
  input  [7:0] from_B_register,
  input  [7:0] from_AC,
  input  Eu,
  input  Su,
  output [7:0] AU_out
);

  wire [7:0] adder_1_out, subtractor_1_out;

  Adder adder_1 (.a(from_B_register), .b(from_AC), .out(adder_1_out), .cin(in_1));  // open: cout
  Subtractor subtractor_1 (.a(from_B_register), .b(from_AC), .out(subtractor_1_out), .bin(in_1));  // open: bout
  Multiplexer #(.width(8)) multiplexer_1 (.in0(adder_1_out), .in1(subtractor_1_out), .out(AU_out), .sel(Su), .en(Eu));
endmodule

module PC (
  input  Cp,
  input  Ep,
  input  reset,
  input  clk,
  output [3:0] to_the_bus
);

  wire half_adder_1_sum, half_adder_2_carry, half_adder_2_sum, half_adder_3_carry, half_adder_3_sum,
       half_adder_4_carry, half_adder_4_sum, not_1_out;
  wire [3:0] d_ff_4_q;

  not not_1 (not_1_out, clk);
  half_adder half_adder_1 (.A(half_adder_2_carry), .B(d_ff_4_q[3]), .sum(half_adder_1_sum));  // open: carry
  D_Flip_Flop d_ff_1 (.clk(not_1_out), .D(half_adder_1_sum), .Q(d_ff_4_q[3]), .reset(reset));  // open: Qn, preset, en
  half_adder half_adder_2 (.A(half_adder_3_carry), .B(d_ff_4_q[2]), .sum(half_adder_2_sum), .carry(half_adder_2_carry));
  D_Flip_Flop d_ff_2 (.clk(not_1_out), .D(half_adder_2_sum), .Q(d_ff_4_q[2]), .reset(reset));  // open: Qn, preset, en
  half_adder half_adder_3 (.A(half_adder_4_carry), .B(d_ff_4_q[1]), .sum(half_adder_3_sum), .carry(half_adder_3_carry));
  D_Flip_Flop d_ff_3 (.clk(not_1_out), .D(half_adder_3_sum), .Q(d_ff_4_q[1]), .reset(reset));  // open: Qn, preset, en
  D_Flip_Flop d_ff_4 (.clk(not_1_out), .D(half_adder_4_sum), .Q(d_ff_4_q[0]), .reset(reset));  // open: Qn, preset, en
  half_adder half_adder_4 (.A(Cp), .B(d_ff_4_q[0]), .sum(half_adder_4_sum), .carry(half_adder_4_carry));
  assign to_the_bus = Ep ? d_ff_4_q : 4'bz;  // Controlled_Buffer controlled_buffer_1
endmodule

module RAM (
  input  [3:0] MAR,
  input  [7:0] Data,
  input  CE,
  output [7:0] bus
);

  wire clock_1_out, not_1_out;

  Clock clock_1 (.out(clock_1_out));
  RAM_part #(.addrWidth(4), .bus("separate")) ram_1 (
    .addr(MAR), .din(Data), .data(bus), .clk(clock_1_out), .ld(not_1_out));  // open: str, sel, clr
  not not_1 (not_1_out, CE);
endmodule

module MAR (
  input  [3:0] from_the_bus,
  input  Lm,
  input  clk,
  input  clear,
  output [3:0] to_RAM
);

  wire not_1_out;
  wire [3:0] controlled_buffer_1_out;

  assign controlled_buffer_1_out = not_1_out ? from_the_bus : 4'bz;  // Controlled_Buffer controlled_buffer_1
  not not_1 (not_1_out, Lm);
  D_Flip_Flop d_ff_1 (.clk(clk), .D(controlled_buffer_1_out[3]), .Q(to_RAM[3]), .reset(clear));  // open: Qn, preset, en
  D_Flip_Flop d_ff_2 (.clk(clk), .D(controlled_buffer_1_out[2]), .Q(to_RAM[2]), .reset(clear));  // open: Qn, preset, en
  D_Flip_Flop d_ff_3 (.clk(clk), .D(controlled_buffer_1_out[1]), .Q(to_RAM[1]), .reset(clear));  // open: Qn, preset, en
  D_Flip_Flop d_ff_4 (.clk(clk), .D(controlled_buffer_1_out[0]), .Q(to_RAM[0]), .reset(clear));  // open: Qn, preset, en
endmodule

// ring
module ring_counter (
  input  clk,
  output T1,
  output T2,
  output T3,
  output T4,
  output T5,
  output T6
);

  wire nor_1_out;

  nor nor_1 (nor_1_out, T1, T2, T3, T4, T5, T6);
  D_Flip_Flop d_ff_1 (.clk(clk), .D(nor_1_out), .Q(T1));  // open: Qn, preset, en, reset
  D_Flip_Flop d_ff_2 (.clk(clk), .D(T1), .Q(T2));  // open: Qn, preset, en, reset
  D_Flip_Flop d_ff_3 (.clk(clk), .D(T2), .Q(T3));  // open: Qn, preset, en, reset
  D_Flip_Flop d_ff_4 (.clk(clk), .D(T3), .Q(T4));  // open: Qn, preset, en, reset
  D_Flip_Flop d_ff_5 (.clk(clk), .D(T4), .Q(T5));  // open: Qn, preset, en, reset
  D_Flip_Flop d_ff_6 (.clk(clk), .D(T5), .Q(T6));  // open: Qn, preset, en, reset
endmodule

module instruction_decoder (
  input  _3,
  input  _2,
  input  _1,
  input  _0,
  output LDA,
  output ADD,
  output SUB,
  output OUT,
  output HLT
);

  wire and_1_out, and_2_out, and_3_out, and_4_out, and_5_out, not_1_out, not_2_out, not_3_out, not_4_out;

  not not_1 (not_1_out, _3);
  not not_2 (not_2_out, _2);
  not not_3 (not_3_out, _1);
  not not_4 (not_4_out, _0);
  and and_1 (and_1_out, not_4_out, not_3_out, not_2_out, not_1_out);
  and and_2 (and_2_out, _0, not_3_out, not_2_out, not_1_out);
  and and_3 (and_3_out, not_4_out, _1, not_2_out, not_1_out);
  and and_4 (and_4_out, not_4_out, _1, _2, _3);
  and and_5 (and_5_out, _0, _1, _2, _3);
  buf buffer_1 (LDA, and_1_out);
  buf buffer_2 (ADD, and_2_out);
  buf buffer_3 (SUB, and_3_out);
  buf buffer_4 (OUT, and_4_out);
  buf buffer_5 (HLT, and_5_out);
endmodule

module controller (
  input  clk,
  input  _3,
  input  _2,
  input  _1,
  input  _0,
  output halt,
  output cp,
  output SU,
  output EA,
  output Lm,
  output Li,
  output Ei,
  output EU,
  output CE,
  output Lb,
  output LA,
  output Lo,
  output ep
);

  wire and_1_out, and_2_out, and_3_out, and_4_out, and_5_out, and_6_out, and_7_out, and_8_out, and_9_out,
       and_10_out, and_11_out, and_12_out, and_15_out, and_16_out, and_17_out, and_18_out, and_19_out,
       instruction_decoder_1_add, instruction_decoder_1_lda, instruction_decoder_1_out,
       instruction_decoder_1_sub, ring_counter_1_t3, ring_counter_1_t4, ring_counter_1_t5, ring_counter_1_t6;

  instruction_decoder instruction_decoder_1 (
    ._3(_3), ._2(_2), ._1(_1), ._0(_0), .LDA(instruction_decoder_1_lda), .ADD(instruction_decoder_1_add),
    .SUB(instruction_decoder_1_sub), .OUT(instruction_decoder_1_out), .HLT(halt));
  ring_counter ring_counter_1 (
    .clk(clk), .T1(ep), .T2(cp), .T3(ring_counter_1_t3), .T4(ring_counter_1_t4), .T5(ring_counter_1_t5),
    .T6(ring_counter_1_t6));
  and and_1 (and_1_out, instruction_decoder_1_lda, ring_counter_1_t4);
  Hex_Digit_Display hex_digit_display_1 (.value({cp, ep, Lm, CE}));  // open: dp
  and and_2 (and_2_out, ring_counter_1_t4, instruction_decoder_1_add);
  and and_3 (and_3_out, ring_counter_1_t4, instruction_decoder_1_sub);
  nor nor_1 (Lm, ep, and_1_out, and_2_out, and_3_out);
  and and_4 (and_4_out, ring_counter_1_t5, instruction_decoder_1_lda);
  and and_5 (and_5_out, ring_counter_1_t5, instruction_decoder_1_add);
  nor nor_2 (CE, ring_counter_1_t3, and_4_out, and_5_out, and_6_out);
  and and_6 (and_6_out, ring_counter_1_t5, instruction_decoder_1_sub);
  not not_1 (Li, ring_counter_1_t3);
  and and_7 (and_7_out, ring_counter_1_t4, instruction_decoder_1_lda);
  and and_8 (and_8_out, ring_counter_1_t4, instruction_decoder_1_add);
  nor nor_3 (Ei, and_7_out, and_8_out, and_9_out);
  and and_9 (and_9_out, ring_counter_1_t4, instruction_decoder_1_sub);
  and and_10 (and_10_out, ring_counter_1_t5, instruction_decoder_1_lda);
  Hex_Digit_Display hex_digit_display_2 (.value({Li, Ei, LA, EA}));  // open: dp
  and and_11 (and_11_out, ring_counter_1_t6, instruction_decoder_1_add);
  and and_12 (and_12_out, ring_counter_1_t6, instruction_decoder_1_sub);
  nor nor_4 (LA, and_10_out, and_11_out, and_12_out);
  and and_13 (SU, ring_counter_1_t6, instruction_decoder_1_sub);
  and and_14 (EA, ring_counter_1_t4, instruction_decoder_1_out);
  and and_15 (and_15_out, ring_counter_1_t6, instruction_decoder_1_add);
  and and_16 (and_16_out, ring_counter_1_t6, instruction_decoder_1_sub);
  or or_1 (EU, and_15_out, and_16_out);
  and and_17 (and_17_out, ring_counter_1_t5, instruction_decoder_1_sub);
  and and_18 (and_18_out, ring_counter_1_t5, instruction_decoder_1_add);
  nor nor_5 (Lb, and_18_out, and_17_out);
  and and_19 (and_19_out, ring_counter_1_t4, instruction_decoder_1_out);
  not not_2 (Lo, and_19_out);
  Hex_Digit_Display hex_digit_display_3 (.value({SU, EU, Lb, Lo}));  // open: dp
endmodule

module main2 (
  input  [3:0] in_1,
  input  in_2,
  input  [7:0] data,
  input  run,
  output [7:0] out_5
);

  wire and_1_out, and_2_out, ce_prime, clear_out, clk, clock_1_out, controller_1_halt, cp, ea, ei_prime, ep,
       eu, la_prime, lb_prime, li_prime, lm_prime, lo_prime, not_1_out, not_2_out, not_3_out, reset, su,
       write_out;
  wire [3:0] IR___controller, mar_1_to_ram, multiplexer_1_out;
  wire [7:0] ac_1_to_add_sub, b_register_1_to_the_alu, output_register_1_to_the_display;

  Button write (.out(write_out));
  and and_1 (and_1_out, write_out, ~run);  // AND_Gate
  Multiplexer #(.width(4)) multiplexer_1 (
    .in0(in_1), .in1(mar_1_to_ram), .out(multiplexer_1_out), .sel(run));  // open: en
  not not_1 (not_1_out, run);
  PC pc_1 (.Cp(cp), .to_the_bus(out_5[3:0]), .Ep(ep), .reset(reset), .clk(clk));
  not not_2 (not_2_out, ce_prime);
  Button clear (.out(clear_out));
  MAR mar_1 (.Lm(lm_prime), .to_RAM(mar_1_to_ram), .clk(clk), .clear(reset), .from_the_bus(out_5[3:0]));
  RAM_part #(.addrWidth(4), .bus("separate")) ram_1 (
    .addr(multiplexer_1_out), .din(data), .data(out_5), .str(not_1_out), .clk(and_1_out), .ld(not_2_out),
    .clr(and_2_out));  // open: sel
  and and_2 (and_2_out, clear_out, ~run);  // AND_Gate
  IR ir_1 (
    .reset(reset), .Ei(ei_prime), .from_the_bus(out_5), .to_the_bus(out_5[3:0]),
    .to_the_controller(IR___controller), .Li(li_prime), .clk(clk));
  AC ac_1 (
    .reset(reset), .from_the_bus(out_5), .to_add_sub(ac_1_to_add_sub), .LA(la_prime), .to_the_bus(out_5),
    .clk(clk), .Ea(ea));
  B_register b_register_1 (
    .Lb(lb_prime), .from_the_bus(out_5), .to_the_ALU(b_register_1_to_the_alu), .reset(reset), .clk(clk));
  output_register output_register_1 (
    .reset(reset), .Lo(lo_prime), .from_the_bus(out_5), .to_the_display(output_register_1_to_the_display),
    .clk(clk));
  ALU alu_1 (
    .AU_out(out_5), .Eu(eu), .Su(su), .from_B_register(b_register_1_to_the_alu), .from_AC(ac_1_to_add_sub),
    .in_1(in_2));
  Hex_Digit_Display hex_digit_display_1 (.value(output_register_1_to_the_display[7:4]));  // open: dp
  Hex_Digit_Display hex_digit_display_2 (.value(output_register_1_to_the_display[3:0]));  // open: dp
  not not_3 (not_3_out, controller_1_halt);
  Clock clock_1 (.out(clock_1_out));
  assign clk = not_3_out ? clock_1_out : 1'bz;  // Controlled_Buffer controlled_buffer_1
  Button u_reset (.out(reset));
  controller controller_1 (
    .halt(controller_1_halt), .EA(ea), .Li(li_prime), .CE(ce_prime), .LA(la_prime), .Lo(lo_prime),
    ._3(IR___controller[3]), ._2(IR___controller[2]), ._1(IR___controller[1]), ._0(IR___controller[0]),
    .cp(cp), .Lm(lm_prime), .Ei(ei_prime), .SU(su), .EU(eu), .Lb(lb_prime), .clk(clk), .ep(ep));
endmodule
