// Logisim project controller.circ as structural Verilog: 2 circuits, main circuit main
module main (
  input  in_1,
  input  in_2,
  input  in_3,
  input  in_4,
  output LDA,
  output ADD,
  output SUB,
  output OUT,
  output HLT
);

  wire and_1_out, and_2_out, and_3_out, and_4_out, and_5_out, not_1_out, not_2_out, not_3_out, not_4_out;

  not not_1 (not_1_out, in_1);
  not not_2 (not_2_out, in_2);
  not not_3 (not_3_out, in_3);
  not not_4 (not_4_out, in_4);
  and and_1 (and_1_out, not_4_out, not_3_out, not_2_out, not_1_out);
  and and_2 (and_2_out, in_4, not_3_out, not_2_out, not_1_out);
  and and_3 (and_3_out, not_4_out, in_3, not_2_out, not_1_out);
  and and_4 (and_4_out, not_4_out, in_3, in_2, in_1);
  and and_5 (and_5_out, in_4, in_3, in_2, in_1);
  buf buffer_1 (LDA, and_1_out);
  buf buffer_2 (ADD, and_2_out);
  buf buffer_3 (SUB, and_3_out);
  buf buffer_4 (OUT, and_4_out);
  buf buffer_5 (HLT, and_5_out);
endmodule

module controller (
);

  main main_1 ();  // open: in_1, in_2, in_3, in_4, LDA, ADD, SUB, OUT, HLT
endmodule
