// Logisim project d&T_flipflop.circ as structural Verilog: 1 circuit, main circuit main
module main (
  input  in_1,
  input  clear,
  input  preset,
  input  enable,
  output q,
  output q_toggled,
  output QT,
  output QbarT
);

  wire clock_1_out;

  Clock clock_1 (.out(clock_1_out));
  D_Flip_Flop d_ff_1 (.clk(clock_1_out), .D(in_1), .Q(q), .Qn(q_toggled), .preset(preset), .en(enable), .reset(clear));
  T_Flip_Flop t_ff_1 (.clk(clock_1_out), .T(in_1), .Q(QT), .Qn(QbarT), .preset(preset), .reset(clear), .en(enable));
endmodule
