// Logisim project d_flipflop.circ as structural Verilog: 1 circuit, main circuit main
module main (
  input  D,
  input  Enable,
  input  Reset,
  output out_4
);

  wire clock_1_out;

  Clock clock_1 (.out(clock_1_out));
  D_Flip_Flop d_ff_1 (.clk(clock_1_out), .D(D), .Q(out_4), .en(Enable), .reset(Reset));  // open: Qn, preset
endmodule
