// Logisim project decade_counter.circ as structural Verilog: 1 circuit, main circuit main
module main (
  input  high,
  input  preset,
  input  enable,
  output [3:0] out_4
);

  wire and_1_out, clock_1_out;

  Clock clock_1 (.out(clock_1_out));
  J_K_Flip_Flop #(.trigger("falling")) j_k_ff_1 (
    .J(high), .clk(clock_1_out), .K(high), .Q(out_4[0]), .preset(preset), .en(enable), .reset(and_1_out));  // open: Qn
  J_K_Flip_Flop #(.trigger("falling")) j_k_ff_2 (
    .J(high), .clk(out_4[0]), .K(high), .Q(out_4[1]), .preset(preset), .en(enable), .reset(and_1_out));  // open: Qn
  J_K_Flip_Flop #(.trigger("falling")) j_k_ff_3 (
    .J(high), .clk(out_4[1]), .K(high), .Q(out_4[2]), .preset(preset), .en(enable), .reset(and_1_out));  // open: Qn
  and and_1 (and_1_out, out_4[1], out_4[3]);
  J_K_Flip_Flop #(.trigger("falling")) j_k_ff_4 (
    .J(high), .clk(out_4[2]), .K(high), .Q(out_4[3]), .preset(preset), .en(enable), .reset(and_1_out));  // open: Qn
endmodule
