// Logisim project falling_edge_asynchronous_counter.circ as structural Verilog: 1 circuit, main circuit main
module main (
  input  in_1,
  input  in_2,
  input  Clear,
  input  Enable,
  input  Preset
);

  wire clock_1_out, j_k_ff_1_q, j_k_ff_2_q, j_k_ff_3_q, j_k_ff_4_q;

  J_K_Flip_Flop #(.trigger("falling")) j_k_ff_1 (
    .J(in_1), .clk(j_k_ff_2_q), .K(in_2), .Q(j_k_ff_1_q), .preset(Preset), .en(Enable), .reset(Clear));  // open: Qn
  J_K_Flip_Flop #(.trigger("falling")) j_k_ff_2 (
    .J(in_1), .clk(j_k_ff_3_q), .K(in_2), .Q(j_k_ff_2_q), .preset(Preset), .en(Enable), .reset(Clear));  // open: Qn
  J_K_Flip_Flop #(.trigger("falling")) j_k_ff_3 (
    .J(in_1), .clk(j_k_ff_4_q), .K(in_2), .Q(j_k_ff_3_q), .preset(Preset), .en(Enable), .reset(Clear));  // open: Qn
  Clock clock_1 (.out(clock_1_out));
  J_K_Flip_Flop #(.trigger("falling")) j_k_ff_4 (
    .J(in_1), .clk(clock_1_out), .K(in_2), .Q(j_k_ff_4_q), .preset(Preset), .en(Enable), .reset(Clear));  // open: Qn
endmodule
