// Logisim project falling_edge_asynchronous_counter2.circ as structural Verilog: 1 circuit, main circuit main
module main (
  input  in_1,
  input  preset,
  input  enable,
  input  reset,
  output out_5,
  output out_6,
  output out_7,
  output out_8
);

  wire clock_1_out;

  J_K_Flip_Flop #(.trigger("falling")) j_k_ff_1 (
    .J(in_1), .clk(out_6), .K(in_1), .Q(out_5), .preset(preset), .en(enable), .reset(reset));  // open: Qn
  J_K_Flip_Flop #(.trigger("falling")) j_k_ff_2 (
    .J(in_1), .clk(out_7), .K(in_1), .Q(out_6), .preset(preset), .en(enable), .reset(reset));  // open: Qn
  J_K_Flip_Flop #(.trigger("falling")) j_k_ff_3 (
    .J(in_1), .clk(out_8), .K(in_1), .Q(out_7), .preset(preset), .en(enable), .reset(reset));  // open: Qn
  Clock clock_1 (.out(clock_1_out));
  J_K_Flip_Flop #(.trigger("falling")) j_k_ff_4 (
    .J(in_1), .clk(clock_1_out), .K(in_1), .Q(out_8), .preset(preset), .en(enable), .reset(reset));  // open: Qn
endmodule
