// Logisim project jk_flipflop.circ as structural Verilog: 1 circuit, main circuit main
module main (
  input  J,
  input  K,
  input  PRESET,
  input  ENABLE,
  input  CLEAR,
  output Q,
  output QBAR
);

  wire clock_1_out;

  Clock clock_1 (.out(clock_1_out));
  J_K_Flip_Flop j_k_ff_1 (
    .J(J), .clk(clock_1_out), .K(K), .Q(Q), .Qn(QBAR), .preset(PRESET), .en(ENABLE), .reset(CLEAR));
endmodule
