// Logisim project program_counter.circ as structural Verilog: 1 circuit, main circuit main
module main (
  input  count,
  input  reset,
  input  enable,
  output [3:0] out_4
);

  wire and_1_out, and_2_out, and_3_out, clock_1_out, j_k_ff_1_q, j_k_ff_2_q, j_k_ff_3_q, j_k_ff_4_q;

  Clock clock_1 (.out(clock_1_out));
  and and_1 (and_1_out, count, and_2_out, j_k_ff_2_q);
  J_K_Flip_Flop j_k_ff_1 (
    .J(and_1_out), .clk(clock_1_out), .K(and_1_out), .Q(j_k_ff_1_q), .reset(reset));  // open: Qn, preset, en
  assign out_4[3] = enable ? j_k_ff_1_q : 1'bz;  // Controlled_Buffer controlled_buffer_1
  and and_2 (and_2_out, count, and_3_out, j_k_ff_3_q);
  J_K_Flip_Flop j_k_ff_2 (
    .J(and_2_out), .clk(clock_1_out), .K(and_2_out), .Q(j_k_ff_2_q), .reset(reset));  // open: Qn, preset, en
  assign out_4[2] = enable ? j_k_ff_2_q : 1'bz;  // Controlled_Buffer controlled_buffer_2
  and and_3 (and_3_out, count, j_k_ff_4_q);
  J_K_Flip_Flop j_k_ff_3 (
    .J(and_3_out), .clk(clock_1_out), .K(and_3_out), .Q(j_k_ff_3_q), .reset(reset));  // open: Qn, preset, en
  assign out_4[1] = enable ? j_k_ff_3_q : 1'bz;  // Controlled_Buffer controlled_buffer_3
  J_K_Flip_Flop j_k_ff_4 (
    .J(count), .clk(clock_1_out), .K(count), .Q(j_k_ff_4_q), .reset(reset));  // open: Qn, preset, en
  assign out_4[0] = enable ? j_k_ff_4_q : 1'bz;  // Controlled_Buffer controlled_buffer_4
endmodule
