// Logisim project r.circ as structural Verilog: 1 circuit, main circuit main
module main (
  input  [3:0] MAR,
  input  [7:0] Data,
  input  Clear,
  input  Store,
  input  Load,
  input  Select,
  output [7:0] MBR
);

  wire clock_1_out;

  Clock clock_1 (.out(clock_1_out));
  RAM #(.addrWidth(4), .bus("separate")) ram_1 (
    .addr(MAR), .din(Data), .data(MBR), .str(Store), .sel(Select), .clk(clock_1_out), .ld(Load), .clr(Clear));
endmodule
