// Logisim project register.circ as structural Verilog: 1 circuit, main circuit main
module main (
  input  Reset,
  output [7:0] Input,
  output [7:0] Output,
  output Enable
);

  wire clock_1_out;

  Register register_1 (.D(Input), .en(Enable), .Q(Output), .clk(clock_1_out), .clr(Reset));
  Clock clock_1 (.out(clock_1_out));
endmodule
