// Logisim project registers_bus.circ as structural Verilog: 1 circuit, main circuit main
module main (
  input  [7:0] in_1,
  input  buffer_enable,
  input  in_3,
  input  Enable,
  input  Clear,
  output [7:0] out_6,
  output [7:0] out_7
);

  wire clock_1_out;
  wire [7:0] controlled_buffer_1_out, register_1_q;

  Clock clock_1 (.out(clock_1_out));
  Register register_1 (.D(in_1), .en(Enable), .Q(register_1_q), .clk(clock_1_out), .clr(Clear));
  assign controlled_buffer_1_out = buffer_enable ? register_1_q : 8'bz;  // Controlled_Buffer controlled_buffer_1
  assign out_6 = in_3 ? controlled_buffer_1_out : 8'bz;  // Controlled_Buffer controlled_buffer_2
  Register register_2 (.D(controlled_buffer_1_out), .en(Enable), .Q(out_7), .clk(clock_1_out), .clr(Clear));
endmodule
