// Logisim project ring_counter.circ as structural Verilog: 1 circuit, main circuit main
module main (
  input  CLR,
  input  Preset
);

  wire clock_1_out, D0_q, D1_q, D2_q, D3_q;

  Clock clock_1 (.out(clock_1_out));
  D_Flip_Flop D3 (.clk(clock_1_out), .D(D2_q), .Q(D3_q), .reset(CLR));  // open: Qn, preset, en
  D_Flip_Flop D2 (.clk(clock_1_out), .D(D1_q), .Q(D2_q), .reset(CLR));  // open: Qn, preset, en
  D_Flip_Flop D1 (.clk(clock_1_out), .D(D0_q), .Q(D1_q), .reset(CLR));  // open: Qn, preset, en
  D_Flip_Flop D0 (.clk(clock_1_out), .D(D3_q), .Q(D0_q), .preset(Preset));  // open: Qn, en, reset
endmodule
