// Logisim project sheet2_practical.circ as structural Verilog: 5 circuits, main circuit main
module main (
  input  SU,
  input  EU,
  input  CE,
  input  Ei,
  input  Li,
  output [3:0] _4_7,
  output [3:0] _0_3
);

  RAM ram_1 (.bus({_4_7, _0_3}), .CE(CE));  // open: MAR, Data
  IR ir_1 (
    .Ei(Ei), .from_the_bus({_4_7, _0_3}), .to_the_bus(_0_3), .Li(Li));  // open: clear, enable, preset, to_the_controller
  ALU alu_1 (.EU(EU), .SU(SU), .to_the_bus({_4_7, _0_3}));  // open: from_B_register, from_the_AC
endmodule

module IR (
  input  clear,
  input  enable,
  input  preset,
  input  Ei,
  input  [7:0] from_the_bus,
  input  Li,
  output [3:0] to_the_bus,
  output [3:0] to_the_controller
);

  wire clk_out, D0, D1, D2, D3, D4, D5, D6, D7, not_1_out, not_2_out, Q0, Q1, Q2, Q3;

  Clock clk (.out(clk_out));
  D_Flip_Flop d_ff_1 (
    .clk(clk_out), .D(D7), .Q(to_the_controller[3]), .preset(preset), .en(enable), .reset(clear));  // open: Qn
  not not_1 (not_1_out, Ei);
  D_Flip_Flop d_ff_2 (
    .clk(clk_out), .D(D6), .Q(to_the_controller[2]), .preset(preset), .en(enable), .reset(clear));  // open: Qn
  assign to_the_bus = not_1_out ? {Q3, Q2, Q1, Q0} : 4'bz;  // Controlled_Buffer controlled_buffer_1
  D_Flip_Flop d_ff_3 (
    .clk(clk_out), .D(D5), .Q(to_the_controller[1]), .preset(preset), .en(enable), .reset(clear));  // open: Qn
  D_Flip_Flop d_ff_4 (
    .clk(clk_out), .D(D4), .Q(to_the_controller[0]), .preset(preset), .en(enable), .reset(clear));  // open: Qn
  D_Flip_Flop d_ff_5 (.clk(clk_out), .D(D3), .Q(Q3), .preset(preset), .en(enable), .reset(clear));  // open: Qn
  D_Flip_Flop d_ff_6 (.clk(clk_out), .D(D2), .Q(Q2), .preset(preset), .en(enable), .reset(clear));  // open: Qn
  D_Flip_Flop d_ff_7 (.clk(clk_out), .D(D1), .Q(Q1), .preset(preset), .en(enable), .reset(clear));  // open: Qn
  D_Flip_Flop d_ff_8 (.clk(clk_out), .D(D0), .Q(Q0), .preset(preset), .en(enable), .reset(clear));  // open: Qn
  assign {D7, D6, D5, D4, D3, D2, D1, D0} = not_2_out ? from_the_bus : 8'bz;  // Controlled_Buffer controlled_buffer_2
  not not_2 (not_2_out, Li);

  // Other names for the same wires on the sheet: Q4 = to_the_controller[0]; Q5 = to_the_controller[1];
  //   Q6 = to_the_controller[2]; Q7 = to_the_controller[3]
endmodule

module ALU (
  input  [7:0] from_B_register,
  input  SU,
  input  [7:0] from_the_AC,
  input  EU,
  output [7:0] to_the_bus
);

  wire full_adder_2_carry_out, full_adder_3_carry_out, full_adder_4_carry_out, full_adder_5_carry_out,
       full_adder_6_carry_out, full_adder_7_carry_out, full_adder_8_carry_out, S0, S1, S2, S3, S4, S5, S6,
       S7, xor_1_out, xor_2_out, xor_3_out, xor_4_out, xor_5_out, xor_6_out, xor_7_out, xor_8_out;

  xor xor_1 (xor_1_out, SU, from_B_register[7]);
  full_adder full_adder_1 (
    .from_the_AC(from_the_AC[7]), .from_B_register(xor_1_out), .carry_in(full_adder_2_carry_out), .sum(S7));  // open: carry_out
  xor xor_2 (xor_2_out, SU, from_B_register[6]);
  full_adder full_adder_2 (
    .from_the_AC(from_the_AC[6]), .from_B_register(xor_2_out), .carry_in(full_adder_3_carry_out), .sum(S6),
    .carry_out(full_adder_2_carry_out));
  assign to_the_bus = EU ? {S7, S6, S5, S4, S3, S2, S1, S0} : 8'bz;  // Controlled_Buffer controlled_buffer_1
  full_adder full_adder_3 (
    .from_the_AC(from_the_AC[5]), .from_B_register(xor_3_out), .carry_in(full_adder_4_carry_out), .sum(S5),
    .carry_out(full_adder_3_carry_out));
  xor xor_3 (xor_3_out, SU, from_B_register[5]);
  full_adder full_adder_4 (
    .from_the_AC(from_the_AC[4]), .from_B_register(xor_4_out), .carry_in(full_adder_5_carry_out), .sum(S4),
    .carry_out(full_adder_4_carry_out));
  xor xor_4 (xor_4_out, SU, from_B_register[4]);
  xor xor_5 (xor_5_out, SU, from_B_register[3]);
  full_adder full_adder_5 (
    .from_the_AC(from_the_AC[3]), .from_B_register(xor_5_out), .carry_in(full_adder_6_carry_out), .sum(S3),
    .carry_out(full_adder_5_carry_out));
  xor xor_6 (xor_6_out, SU, from_B_register[2]);
  full_adder full_adder_6 (
    .from_the_AC(from_the_AC[2]), .from_B_register(xor_6_out), .carry_in(full_adder_7_carry_out), .sum(S2),
    .carry_out(full_adder_6_carry_out));
  xor xor_7 (xor_7_out, SU, from_B_register[1]);
  full_adder full_adder_7 (
    .from_the_AC(from_the_AC[1]), .from_B_register(xor_7_out), .carry_in(full_adder_8_carry_out), .sum(S1),
    .carry_out(full_adder_7_carry_out));
  xor xor_8 (xor_8_out, SU, from_B_register[0]);
  full_adder full_adder_8 (
    .from_the_AC(from_the_AC[0]), .from_B_register(xor_8_out), .carry_in(SU), .sum(S0),
    .carry_out(full_adder_8_carry_out));
endmodule

// full-A
module full_adder (
  input  from_the_AC,
  input  from_B_register,
  input  carry_in,
  output sum,
  output carry_out
);

  wire and_1_out, and_2_out, xor_1_out;

  xor xor_1 (xor_1_out, from_the_AC, from_B_register);
  and and_1 (and_1_out, from_the_AC, from_B_register);
  xor xor_2 (sum, xor_1_out, carry_in);
  and and_2 (and_2_out, xor_1_out, carry_in);
  or or_1 (carry_out, and_1_out, and_2_out);
endmodule

module RAM (
  input  [3:0] MAR,
  input  [7:0] Data,
  input  CE,
  output [7:0] bus
);

  wire clock_1_out, not_1_out;

  Clock clock_1 (.out(clock_1_out));
  RAM_part #(.addrWidth(4), .bus("separate")) ram_1 (
    .addr(MAR), .din(Data), .data(bus), .clk(clock_1_out), .ld(not_1_out));  // open: str, sel, clr
  not not_1 (not_1_out, CE);
endmodule
