// Logisim project shift_registerr.circ as structural Verilog: 1 circuit, main circuit main
module main (
  input  Input,
  input  Enable,
  input  Preset,
  input  Clear,
  output Output
);

  wire clock_1_out, d_ff_1_q, d_ff_2_q, d_ff_3_q;

  Clock clock_1 (.out(clock_1_out));
  D_Flip_Flop d_ff_1 (
    .clk(clock_1_out), .D(Input), .Q(d_ff_1_q), .preset(Preset), .en(Enable), .reset(Clear));  // open: Qn
  D_Flip_Flop d_ff_2 (
    .clk(clock_1_out), .D(d_ff_1_q), .Q(d_ff_2_q), .preset(Preset), .en(Enable), .reset(Clear));  // open: Qn
  D_Flip_Flop d_ff_3 (
    .clk(clock_1_out), .D(d_ff_2_q), .Q(d_ff_3_q), .preset(Preset), .en(Enable), .reset(Clear));  // open: Qn
  D_Flip_Flop d_ff_4 (
    .clk(clock_1_out), .D(d_ff_3_q), .Q(Output), .preset(Preset), .en(Enable), .reset(Clear));  // open: Qn
endmodule
