// Logisim project synchronous_ring_counter.circ as structural Verilog: 1 circuit, main circuit main
module main (
  input  enable,
  input  clear,
  input  preset
);

  wire clock_1_out, D0_q, D1_q, D2_q, D3_q;

  Clock clock_1 (.out(clock_1_out));
  D_Flip_Flop #(.trigger("falling")) D0 (
    .clk(clock_1_out), .D(D3_q), .Q(D0_q), .preset(preset), .en(enable));  // open: Qn, reset
  D_Flip_Flop #(.trigger("falling")) D1 (
    .clk(clock_1_out), .D(D0_q), .Q(D1_q), .en(enable), .reset(clear));  // open: Qn, preset
  D_Flip_Flop #(.trigger("falling")) D2 (
    .clk(clock_1_out), .D(D1_q), .Q(D2_q), .en(enable), .reset(clear));  // open: Qn, preset
  D_Flip_Flop #(.trigger("falling")) D3 (
    .clk(clock_1_out), .D(D2_q), .Q(D3_q), .en(enable), .reset(clear));  // open: Qn, preset
endmodule
