// Logisim project universal_counter.circ as structural Verilog: 3 circuits, main circuit main
module main (
  input  in_1,
  input  high,
  input  enable,
  input  clear,
  input  preset,
  output [3:0] out_6
);

  wire _1_2_out, _1_3_out, _1_out, _2_2_out, _2_3_out, _2_out, _3_2_out, _3_3_out, _3_out, clock_1_out,
       j_k_ff_1_qn, j_k_ff_2_qn, j_k_ff_3_qn, not_1_out;

  Clock clock_1 (.out(clock_1_out));
  not not_1 (not_1_out, in_1);
  and _1 (_1_out, not_1_out, out_6[0]);
  J_K_Flip_Flop #(.trigger("falling")) j_k_ff_1 (
    .J(high), .clk(clock_1_out), .K(high), .Q(out_6[0]), .Qn(j_k_ff_1_qn), .preset(preset), .en(enable),
    .reset(clear));
  and _2 (_2_out, in_1, j_k_ff_1_qn);
  or _3 (_3_out, _1_out, _2_out);
  J_K_Flip_Flop #(.trigger("falling")) j_k_ff_2 (
    .J(high), .clk(_3_out), .K(high), .Q(out_6[1]), .Qn(j_k_ff_2_qn), .preset(preset), .en(enable),
    .reset(clear));
  and _1_2 (_1_2_out, not_1_out, out_6[1]);
  and _2_2 (_2_2_out, in_1, j_k_ff_2_qn);
  or _3_2 (_3_2_out, _1_2_out, _2_2_out);
  J_K_Flip_Flop #(.trigger("falling")) j_k_ff_3 (
    .J(high), .clk(_3_2_out), .K(high), .Q(out_6[2]), .Qn(j_k_ff_3_qn), .preset(preset), .en(enable),
    .reset(clear));
  and _1_3 (_1_3_out, not_1_out, out_6[2]);
  and _2_3 (_2_3_out, in_1, j_k_ff_3_qn);
  J_K_Flip_Flop #(.trigger("falling")) j_k_ff_4 (
    .J(high), .clk(_3_3_out), .K(high), .Q(out_6[3]), .preset(preset), .en(enable), .reset(clear));  // open: Qn
  or _3_3 (_3_3_out, _1_3_out, _2_3_out);
endmodule

module decade_counter (
  input  high,
  input  preset,
  input  enable,
  output [3:0] out_4
);

  wire and_1_out, clock_1_out;

  Clock clock_1 (.out(clock_1_out));
  J_K_Flip_Flop #(.trigger("falling")) j_k_ff_1 (
    .J(high), .clk(clock_1_out), .K(high), .Q(out_4[0]), .preset(preset), .en(enable), .reset(and_1_out));  // open: Qn
  J_K_Flip_Flop #(.trigger("falling")) j_k_ff_2 (
    .J(high), .clk(out_4[0]), .K(high), .Q(out_4[1]), .preset(preset), .en(enable), .reset(and_1_out));  // open: Qn
  J_K_Flip_Flop #(.trigger("falling")) j_k_ff_3 (
    .J(high), .clk(out_4[1]), .K(high), .Q(out_4[2]), .preset(preset), .en(enable), .reset(and_1_out));  // open: Qn
  and and_1 (and_1_out, out_4[1], out_4[3]);
  J_K_Flip_Flop #(.trigger("falling")) j_k_ff_4 (
    .J(high), .clk(out_4[2]), .K(high), .Q(out_4[3]), .preset(preset), .en(enable), .reset(and_1_out));  // open: Qn
endmodule

module universal_counter (
  input  high,
  input  clear,
  input  enable,
  input  preset,
  input  selection,
  input  enable_2,
  output [3:0] out_7
);

  wire [3:0] Decade_out_4, Up_Down_out_6;

  main Up_Down (.high(high), .clear(clear), .preset(preset), .enable(enable), .out_6(Up_Down_out_6));  // open: in_1
  decade_counter Decade (.high(high), .preset(preset), .enable(enable), .out_4(Decade_out_4));
  Multiplexer #(.width(4)) multiplexer_1 (
    .in0(Up_Down_out_6), .in1(Decade_out_4), .out(out_7), .sel(selection), .en(enable_2));
endmodule
