// Logisim project up_down_asynchronous.circ as structural Verilog: 1 circuit, main circuit main
module main (
  input  in_1,
  input  high,
  input  enable,
  input  clear,
  input  preset,
  output [3:0] out_6
);

  wire _1_2_out, _1_3_out, _1_out, _2_2_out, _2_3_out, _2_out, _3_2_out, _3_3_out, _3_out, clock_1_out,
       j_k_ff_1_qn, j_k_ff_2_qn, j_k_ff_3_qn, not_1_out;

  Clock clock_1 (.out(clock_1_out));
  not not_1 (not_1_out, in_1);
  and _1 (_1_out, not_1_out, out_6[0]);
  J_K_Flip_Flop #(.trigger("falling")) j_k_ff_1 (
    .J(high), .clk(clock_1_out), .K(high), .Q(out_6[0]), .Qn(j_k_ff_1_qn), .preset(preset), .en(enable),
    .reset(clear));
  and _2 (_2_out, in_1, j_k_ff_1_qn);
  or _3 (_3_out, _1_out, _2_out);
  J_K_Flip_Flop #(.trigger("falling")) j_k_ff_2 (
    .J(high), .clk(_3_out), .K(high), .Q(out_6[1]), .Qn(j_k_ff_2_qn), .preset(preset), .en(enable),
    .reset(clear));
  and _1_2 (_1_2_out, not_1_out, out_6[1]);
  and _2_2 (_2_2_out, in_1, j_k_ff_2_qn);
  or _3_2 (_3_2_out, _1_2_out, _2_2_out);
  J_K_Flip_Flop #(.trigger("falling")) j_k_ff_3 (
    .J(high), .clk(_3_2_out), .K(high), .Q(out_6[2]), .Qn(j_k_ff_3_qn), .preset(preset), .en(enable),
    .reset(clear));
  and _1_3 (_1_3_out, not_1_out, out_6[2]);
  and _2_3 (_2_3_out, in_1, j_k_ff_3_qn);
  J_K_Flip_Flop #(.trigger("falling")) j_k_ff_4 (
    .J(high), .clk(_3_3_out), .K(high), .Q(out_6[3]), .preset(preset), .en(enable), .reset(clear));  // open: Qn
  or _3_3 (_3_3_out, _1_3_out, _2_3_out);
endmodule
